# Fritzing sketch quizboard_2_0 (saved by Fritzing 0.9.3b)
circuit board: 8.46667cm x 5.64444cm
circuit board: 1.39778cm x 2.3706cm
circuit board: 1.39778cm x 2.3706cm
breadboards: 3

parts:
  Bauteil1 = Arduino Uno (Rev3)
  LED_Shifter = HEF4094 [package="DIP16 [THT]"]
  R1 = Resistor [tolerance=±5% resistance=220 package=THT]
  R2 = Resistor [tolerance=±5% resistance=220 package=THT]
  R3 = Resistor [tolerance=±5% resistance=220 package=THT]
  R4 = Resistor [tolerance=±5% resistance=220 package=THT]
  R5 = Resistor [tolerance=±5% resistance=220 package=THT]
  R6 = Resistor [tolerance=±5% resistance=220 package=THT]
  R7 = Resistor [tolerance=±5% resistance=220 package=THT]
  R8 = Resistor [tolerance=±5% resistance=220 package=THT]
  S1 = Pushbutton [package=THT]
  LED1 = LED - 5mm [color="Green (565nm)" package="5 mm [THT]"]
  Hot_Plugs = female pin header, 8 pins [form="♀ (female)"]
  Kont_B = rounded female pin header, 4 pins [form="♀ (female rounded)"]
  Kont_C = rounded female pin header, 4 pins [form="♀ (female rounded)"]
  R37 = Resistor [tolerance=±5% resistance=10M package=THT]
  Kont_A = rounded female pin header, 4 pins [form="♀ (female rounded)"]
  R38 = Resistor [tolerance=±5% resistance=10M package=THT]
  Kont_D = rounded female pin header, 4 pins [form="♀ (female rounded)"]
  R39 = Resistor [tolerance=±5% resistance=10M package=THT]
  R40 = Resistor [tolerance=±5% resistance=10M package=THT]
  Sensor_Buchse = female pin header, 4 pins [form="♀ (female)"]
  R20 = Resistor [tolerance=±5% resistance=1M package=THT]
  R19 = Resistor [tolerance=±5% resistance=1M package=THT]
  R18 = Resistor [tolerance=±5% resistance=1M package=THT]
  R17 = Resistor [tolerance=±5% resistance=1M package=THT]
  R32 = Resistor [tolerance=±5% resistance=1M package=THT]
  R36 = Resistor [tolerance=±5% resistance=1M package=THT]
  R34 = Resistor [tolerance=±5% resistance=1M package=THT]
  R35 = Resistor [tolerance=±5% resistance=1M package=THT]
  R31 = Resistor [tolerance=±5% resistance=1M package=THT]
  R30 = Resistor [tolerance=±5% resistance=1M package=THT]
  R33 = Resistor [tolerance=±5% resistance=1M package=THT]
  R25 = Resistor [tolerance=±5% resistance=1M package=THT]
  7_Segment1 = 7 Segment Display  # not connected
  U1 = 74HC595 [package="DIP16 [THT]"]
  LED_Stecker = male pin header, 5 pins [form="♂ (male)"]
  LED_Bus = rounded female pin header, 5 pins [form="♀ (female rounded)"]
  LED2 = LED - 5mm [color="Green (565nm)" package="5 mm [THT]"]
  LED3 = LED - 5mm [color="Green (565nm)" package="5 mm [THT]"]
  LED4 = LED - 5mm [color="Green (565nm)" package="5 mm [THT]"]
  LED5 = LED - 5mm [color="Green (565nm)" package="5 mm [THT]"]
  LED6 = LED - 5mm [color="Green (565nm)" package="5 mm [THT]"]
  LED7 = LED - 5mm [color="Green (565nm)" package="5 mm [THT]"]
  LED8 = LED - 5mm [color="Green (565nm)" package="5 mm [THT]"]

nets:
  N1: Bauteil1.A0, R37.Pin_1, Kont_A.pin1, Sensor_Buchse.pin4, R17.Pin_0, R33.Pin_1
  N2: Bauteil1.A1, Kont_B.pin1, R38.Pin_1, Sensor_Buchse.pin3, R18.Pin_0, R30.Pin_1
  N3: Bauteil1.A2, Kont_C.pin1, R39.Pin_1, Sensor_Buchse.pin2, R19.Pin_0, R31.Pin_1
  N4: Bauteil1.A3, Kont_D.pin1, R40.Pin_1, Sensor_Buchse.pin1, R20.Pin_0, R32.Pin_1
  N5: Bauteil1.D10_PWM/SS, U1.DS, LED_Stecker.pin5, LED_Bus.pin5
  N6: Bauteil1.D11_PWM/MOSI, U1.ST_CP, LED_Stecker.pin3, LED_Bus.pin3
  N7: Bauteil1.D12/MISO, U1.SH_CP, LED_Stecker.pin2, LED_Bus.pin2
  GND: Bauteil1.GND, LED_Shifter.Vss, LED1.anode, R20.Pin_1, R19.Pin_1, R18.Pin_1, R17.Pin_1, U1.GND, U1.OE, LED_Stecker.pin4, LED_Bus.pin4, LED2.anode, LED3.anode, LED4.anode, LED5.anode, LED6.anode, LED7.anode, LED8.anode
  N8: Bauteil1.D0/RX, LED_Shifter.CLOCK
  N9: Bauteil1.D1/TX, LED_Shifter.DATA
  N10: Bauteil1.D2, LED_Shifter.STROBE
  5V: Bauteil1.5V, LED_Shifter.OE, LED_Shifter.Vdd, S1.leg1, Hot_Plugs.pin1, U1.MR, U1.VCC, LED_Stecker.pin1, LED_Bus.pin1
  N11: R1.Pin_0, U1.Q7
  N12: R1.Pin_1, LED8.cathode
  N13: R2.Pin_0, U1.Q6
  N14: R2.Pin_1, LED7.cathode
  N15: R3.Pin_0, U1.Q5
  N16: R3.Pin_1, LED6.cathode
  N17: R4.Pin_0, U1.Q4
  N18: R4.Pin_1, LED5.cathode
  N19: R5.Pin_0, U1.Q3
  N20: R5.Pin_1, LED4.cathode
  N21: R6.Pin_0, U1.Q2
  N22: R6.Pin_1, LED3.cathode
  N23: R7.Pin_0, U1.Q0
  N24: R7.Pin_1, LED1.cathode
  N25: R8.Pin_0, U1.Q1
  N26: R8.Pin_1, LED2.cathode
  N27: Kont_B.pin2, R34.Pin_0, R30.Pin_0
  N28: Kont_B.pin3, R34.Pin_1
  N29: Kont_B.pin4, R38.Pin_0
  N30: Kont_C.pin2, R35.Pin_0, R31.Pin_0
  N31: Kont_C.pin3, R35.Pin_1
  N32: Kont_C.pin4, R39.Pin_0
  N33: R37.Pin_0, Kont_A.pin4
  N34: Kont_A.pin2, R33.Pin_0, R25.Pin_0
  N35: Kont_A.pin3, R25.Pin_1
  N36: Kont_D.pin2, R32.Pin_0, R36.Pin_0
  N37: Kont_D.pin3, R36.Pin_1
  N38: Kont_D.pin4, R40.Pin_0
